// Logisim project 1.circ as structural Verilog: 1 circuit, main circuit main
module main (
  input  sensor1,
  input  sensor2,
  input  sensor3,
  output heater
);

  wire nor_1_out, nor_2_out, nor_3_out;

  nor nor_1 (nor_1_out, sensor1, sensor2);
  not nor_2 (nor_2_out, nor_1_out);  // NOR_Gate
  nor nor_3 (nor_3_out, nor_2_out, sensor3);
  not nor_4 (heater, nor_3_out);  // NOR_Gate
endmodule
