// Logisim project 10.circ as structural Verilog: 1 circuit, main circuit main
module main (
  input  in_1,
  input  in_2,
  input  in_3,
  input  in_4,
  output out_5,
  output out_6,
  output out_7,
  output out_8
);

  wire nor_1_out, nor_2_out, nor_3_out, nor_4_out, nor_5_out, not_2_out, not_3_out;

  Hex_Digit_Display hex_digit_display_1 (.value({in_4, in_3, in_2, in_1}));  // open: dp
  not not_1 (out_5, in_1);
  not not_2 (not_2_out, in_1);
  nor nor_1 (nor_1_out, not_2_out, in_2);
  not not_3 (not_3_out, in_2);
  nor nor_2 (nor_2_out, nor_1_out, nor_3_out);
  nor nor_3 (nor_3_out, in_1, not_3_out);
  not not_4 (out_6, nor_2_out);
  nor nor_4 (nor_4_out, out_5, out_6, out_7);
  xor xor_1 (out_8, nor_4_out, in_4);
  nor nor_5 (nor_5_out, out_5, out_6);
  xor xor_2 (out_7, nor_5_out, in_3);
  Hex_Digit_Display hex_digit_display_2 (.value({out_8, out_7, out_6, out_5}));  // open: dp
endmodule
