// Logisim project 9.2.circ as structural Verilog: 1 circuit, main circuit main
module main (
  input  in_1,
  input  in_2,
  input  in_3,
  input  in_4,
  input  in_5,
  input  in_6
);

  wire and_1_out, nor_2_out, not_1_out, or_1_out;

  or or_1 (or_1_out, in_1, in_2);
  and and_1 (and_1_out, in_1, in_2);
  not not_1 (not_1_out, or_1_out);
  // NOR_Gate nor_1 has open pins: in0=in_5, in1=in_6, out=open
  nor nor_2 (nor_2_out, not_1_out, in_3);
endmodule
